// Logisim project TASK2.circ as structural Verilog: 1 circuit, main circuit main
module main (
  input  A1,
  input  A0,
  input  B1,
  input  B0,
  output Y0
);

  wire n3_to_8_decoder_74138_1_p5, n3_to_8_decoder_74138_1_p6, n3_to_8_decoder_74138_1_p7,
       n3_to_8_decoder_74138_2_p6, n3_to_8_decoder_74138_2_p7, n3_to_8_decoder_74138_2_p8,
       n3_to_8_decoder_74138_2_p9, n3_to_8_decoder_74138_2_p10, n3_to_8_decoder_74138_2_p11,
       n3_to_8_decoder_74138_2_p13, nand_2_out, not_2_out, or_1_out;

  // _3_to_8_decoder__74138 #(.Facing("east")) 3_to_8_decoder_74138_1: pin names not known; wires that end beside it: A1, B0, B1, A0, n3_to_8_decoder_74138_1_p5, n3_to_8_decoder_74138_1_p6, n3_to_8_decoder_74138_1_p7
  // NOT_Gate not_1 has open pins: in=1'b1, out=open
  not not_2 (not_2_out, A1);
  // _3_to_8_decoder__74138 #(.Facing("east")) 3_to_8_decoder_74138_2: pin names not known; wires that end beside it: B0, B1, A0, not_2_out, A1, n3_to_8_decoder_74138_2_p6, n3_to_8_decoder_74138_2_p7, n3_to_8_decoder_74138_2_p8, n3_to_8_decoder_74138_2_p9, n3_to_8_decoder_74138_2_p10, n3_to_8_decoder_74138_2_p11, n3_to_8_decoder_74138_2_p9, n3_to_8_decoder_74138_2_p13
  not not_3 (n3_to_8_decoder_74138_2_p6, 1'b1);
  not not_4 (n3_to_8_decoder_74138_2_p7, 1'b1);
  not not_5 (n3_to_8_decoder_74138_2_p8, 1'b1);
  nand nand_1 (n3_to_8_decoder_74138_1_p7, n3_to_8_decoder_74138_1_p5, n3_to_8_decoder_74138_1_p6);
  nand nand_2 (nand_2_out, n3_to_8_decoder_74138_2_p9, n3_to_8_decoder_74138_2_p10);
  not not_6 (n3_to_8_decoder_74138_2_p13, n3_to_8_decoder_74138_2_p11);
  or or_1 (or_1_out, n3_to_8_decoder_74138_1_p7, nand_2_out);
  or or_2 (Y0, or_1_out, n3_to_8_decoder_74138_2_p13);
endmodule
