// Logisim project lab2.circ as structural Verilog: 1 circuit, main circuit main
module main (
  input  A1,
  input  A0,
  input  B1,
  input  S,
  input  B0,
  output Y1,
  output Y0
);

  wire n3_to_8_decoder_74138_1_p4, n3_to_8_decoder_74138_1_p5, n3_to_8_decoder_74138_1_p6,
       n3_to_8_decoder_74138_1_p7, n3_to_8_decoder_74138_1_p8, n3_to_8_decoder_74138_2_p6,
       n3_to_8_decoder_74138_2_p7, n3_to_8_decoder_74138_2_p10, n3_to_8_decoder_74138_2_p11,
       n3_to_8_decoder_74138_2_p12, n3_to_8_decoder_74138_2_p13, n3_to_8_decoder_74138_2_p14,
       n3_to_8_decoder_74138_2_p15, n3_to_8_decoder_74138_2_p16, n3_to_8_decoder_74138_2_p17,
       n4_to_1_mux_x2_74153_1_p8, nand_1_out, nand_2_out, nand_3_out, nand_4_out, nand_5_out, nand_6_out,
       nand_7_out, nand_8_out, not_1_out, not_4_out, not_5_out, not_6_out, not_7_out, or_1_out, or_2_out,
       or_3_out, or_4_out, or_5_out, or_6_out;

  not not_1 (not_1_out, A1);
  // _3_to_8_decoder__74138 #(.Facing("east")) 3_to_8_decoder_74138_1: pin names not known; wires that end beside it: B0, B1, A0, n3_to_8_decoder_74138_1_p4, n3_to_8_decoder_74138_1_p5, n3_to_8_decoder_74138_1_p6, n3_to_8_decoder_74138_1_p7, n3_to_8_decoder_74138_1_p8
  // _3_to_8_decoder__74138 #(.Facing("east")) 3_to_8_decoder_74138_2: pin names not known; wires that end beside it: B0, B1, A0, not_1_out, A1, n3_to_8_decoder_74138_2_p6, n3_to_8_decoder_74138_2_p7, n3_to_8_decoder_74138_2_p6, n3_to_8_decoder_74138_2_p7, n3_to_8_decoder_74138_2_p10, n3_to_8_decoder_74138_2_p11, n3_to_8_decoder_74138_2_p12, n3_to_8_decoder_74138_2_p13, n3_to_8_decoder_74138_2_p14, n3_to_8_decoder_74138_2_p15, n3_to_8_decoder_74138_2_p16, n3_to_8_decoder_74138_2_p17
  not not_2 (n3_to_8_decoder_74138_2_p6, 1'b1);
  not not_3 (n3_to_8_decoder_74138_2_p7, 1'b1);
  nand nand_1 (nand_1_out, n3_to_8_decoder_74138_1_p8, n3_to_8_decoder_74138_1_p7);
  not not_4 (not_4_out, n3_to_8_decoder_74138_2_p16);
  nand nand_2 (nand_2_out, n3_to_8_decoder_74138_1_p5, n3_to_8_decoder_74138_1_p7);
  nand nand_3 (nand_3_out, n3_to_8_decoder_74138_2_p11, n3_to_8_decoder_74138_2_p14);
  nand nand_4 (nand_4_out, n3_to_8_decoder_74138_2_p10, n3_to_8_decoder_74138_2_p12);
  or or_1 (or_1_out, nand_1_out, nand_4_out);
  or or_2 (or_2_out, nand_2_out, nand_3_out);
  nand nand_5 (nand_5_out, n3_to_8_decoder_74138_1_p4, n3_to_8_decoder_74138_1_p6);
  nand nand_6 (nand_6_out, n3_to_8_decoder_74138_2_p10, n3_to_8_decoder_74138_2_p13);
  not not_5 (not_5_out, n3_to_8_decoder_74138_2_p15);
  nand nand_7 (nand_7_out, n3_to_8_decoder_74138_2_p15, n3_to_8_decoder_74138_2_p17);
  or or_3 (or_3_out, not_4_out, or_2_out);
  or or_4 (or_4_out, nand_5_out, nand_6_out);
  or or_5 (or_5_out, or_4_out, not_5_out);
  or or_6 (or_6_out, nand_7_out, or_1_out);
  not not_6 (not_6_out, nand_8_out);
  nand nand_8 (nand_8_out, A1, B1);
  not not_7 (not_7_out, 1'b1);
  // _4_to_1_MUX__x2___74153 #(.Facing("east")) 4_to_1_mux_x2_74153_1: pin names not known; wires that end beside it: not_6_out, or_3_out, or_6_out, or_5_out, not_7_out, S, not_7_out, n4_to_1_mux_x2_74153_1_p8, Y1, Y0
  not not_8 (n4_to_1_mux_x2_74153_1_p8, 1'b1);
endmodule
