// Logisim project task1.circ as structural Verilog: 1 circuit, main circuit main
module main (
  input  A1,
  input  A0,
  input  B1,
  input  B0,
  output Y0,
  output Y1
);

  wire and_1_out, and_3_out, not_1_out, not_2_out, or_1_out, or_2_out, or_3_out, or_4_out;

  not not_1 (not_1_out, A1);
  not not_2 (not_2_out, B1);
  or or_1 (or_1_out, not_1_out, B0);
  or or_2 (or_2_out, A1, A0);
  or or_3 (or_3_out, A0, not_2_out);
  or or_4 (or_4_out, B1, B0);
  and and_1 (and_1_out, or_1_out, or_2_out);
  and and_2 (Y0, and_1_out, and_3_out);
  and and_3 (and_3_out, or_3_out, or_4_out);
  and and_4 (Y1, B1, A1);
endmodule
